# Fritzing sketch uWaiPi Board Design (saved by Fritzing 0.9.3b)
circuit board: 8.46667cm x 5.64444cm
stripboards: 2

parts:
  R1 = Resistor [tolerance=±5% resistance=10k package="2512 [SMD]"]
  R2 = Resistor [tolerance=±5% resistance=10k package="2512 [SMD]"]
  R3 = Resistor [tolerance=±5% resistance=10k package="2512 [SMD]"]
  R4 = Resistor [tolerance=±5% resistance=1.5k package="2512 [SMD]"]
  R5 = Resistor [tolerance=±5% resistance=1.5k package="2512 [SMD]"]
  R6 = Resistor [tolerance=±5% resistance=1.5k package="2512 [SMD]"]
  JP8 = Header 1 [package=1x01_offset]
  JP9 = Header 1 [package=1x01_offset]
  JP10 = Header 1 [package=1x01_offset]
  JP11 = Header 1 [package=1x01_offset]
  JP12 = Header 1 [package=1x01_offset]
  JP13 = Header 1 [package=1x01_offset]
  JP14 = Header 1 [package=1x01_offset]
  JP15 = Header 1 [package=1x01_offset]
  JP16 = Header 1 [package=1x01_offset]
  C1 = Electrolytic Capacitor [capacitance=100nF voltage=10V package="0807 [SMD, electrolytic]"]
  C2 = Electrolytic Capacitor [capacitance=100nF voltage=10V package="0807 [SMD, electrolytic]"]
  C3 = Electrolytic Capacitor [capacitance=100nF voltage=10V package="0807 [SMD, electrolytic]"]
  Raspberry_Pi_Zero = Raspberry Pi Zero
  16x02_LCD_Display = LCD-16X2 [package=lcd-16x2_noholes]
  part = LCM1602 IIC [part_number="LCM1602 IIC" chip_label="LCM1602 IIC" package="DIP (Dual Inline) [THT]"]
  Q2 = TRANSISTOR_NPN [part_number=2N2222 package=to-92-ammo]
  Q3 = TRANSISTOR_NPN [part_number=2N2222 package=to-92-ammo]
  JP17 = Header 1 [package=1x01_offset]
  JP18 = Header 1 [package=1x01_offset]
  R8 = Resistor [tolerance=±5% resistance=1k package="2512 [SMD]"]
  D1 = Schottky Diode [part_number=IN4002 package="Melf DO-213 AB [SMD]"]
  JP19 = Header 1 [package=1x01_offset]
  JP20 = Header 1 [package=1x01_offset]
  JP21 = Header 1 [package=1x01_offset]
  JP22 = Header 1 [package=1x01_offset]
  JP23 = Header 1 [package=1x01_offset]
  JP24 = Header 1 [package=1x01_offset]
  JP25 = Header 1 [package=1x01_offset]
  JP26 = Header 1 [package=1x01_offset]
  C5 = Ceramic Capacitor [capacitance=10nF package="1206 [SMD, multilayer]"]
  C6 = Electrolytic Capacitor [capacitance=1µF voltage=10V package="0807 [SMD, electrolytic]"]
  C7 = Ceramic Capacitor [capacitance=1nF package="1206 [SMD, multilayer]"]
  JP28 = Header 1 [package=1x01_offset]
  JP29 = Header 1 [package=1x01_offset]
  Push_Button = Round Pushbutton
  Push_Button_2 = Round Pushbutton
  Push_Button_3 = Round Pushbutton
  Water_Pump = DC Motor
  JP27 = Header 1 [package=1x01_offset]
  JP30 = Header 1 [package=1x01_offset]
  JP31 = Header 1 [package=1x01_offset]
  JP32 = Header 1 [package=1x01_offset]
  JP33 = Header 1 [package=1x01_offset]
  JP34 = Header 1 [package=1x01_offset]
  R7 = Resistor [tolerance=±5% resistance=1k package="2512 [SMD]"]
  C8 = Electrolytic Capacitor [capacitance=1μF voltage=10V package="0405 [SMD, electrolytic]"]

nets:
  GND: R1.Pin_0, R2.Pin_0, R3.Pin_0, Raspberry_Pi_Zero.GND, part.GND, Q3.E, JP22.1, JP25.1, C5.1, C6.-, C7.1, JP31.1, JP32.1
  N1: R1.Pin_1, R4.Pin_0, JP12.1, C1.-, Push_Button_2.leg0
  N2: R2.Pin_1, R5.Pin_0, JP14.1, C2.-, Push_Button.leg0
  N3: R3.Pin_1, R6.Pin_0, JP16.1, C3.-, Push_Button_3.leg0
  N4: R4.Pin_1, JP8.1, Raspberry_Pi_Zero.GPIO17
  N5: R5.Pin_1, JP9.1, Raspberry_Pi_Zero.GPIO27
  N6: R6.Pin_1, JP10.1, Raspberry_Pi_Zero.GPIO22
  3V3: JP11.1, JP13.1, JP15.1, C1.+, C2.+, C3.+, Raspberry_Pi_Zero.3v3, Raspberry_Pi_Zero.3V3, Push_Button.leg1, Push_Button_2.leg1, Push_Button_3.leg1, JP34.1
  N7: Raspberry_Pi_Zero.GPIO2, part.SDA, JP20.1, JP23.1
  N8: Raspberry_Pi_Zero.GPIO3, part.SCL, JP19.1, JP24.1
  N9: Raspberry_Pi_Zero.GPIO4, R8.Pin_0, JP33.1
  N10: Raspberry_Pi_Zero.GPIO18, JP29.1, R7.Pin_1
  5V: Raspberry_Pi_Zero.5V, part.VCC, JP18.1, D1.cathode, JP21.1, JP26.1, C5.0, C6.+, C7.0, Water_Pump.pin_2, JP30.1, C8.+
  VSS: 16x02_LCD_Display.VSS, part.VSS
  VDD: 16x02_LCD_Display.VDD, part.VDD
  N11: 16x02_LCD_Display.VO, part.V0
  N12: 16x02_LCD_Display.RS, part.RS
  N13: 16x02_LCD_Display.R_W, part.RW
  N14: 16x02_LCD_Display.E, part.E
  N15: 16x02_LCD_Display.DB0, part.D0
  N16: 16x02_LCD_Display.DB1, part.D1
  N17: 16x02_LCD_Display.DB2, part.D2
  N18: 16x02_LCD_Display.DB3, part.D3
  N19: 16x02_LCD_Display.DB4, part.D4
  N20: 16x02_LCD_Display.DB5, part.D5
  N21: 16x02_LCD_Display.DB6, part.D6
  N22: 16x02_LCD_Display.DB7, part.D7
  N23: 16x02_LCD_Display.A, part.A
  N24: 16x02_LCD_Display.K, part.K
  N25: part.LED_A, Q2.E, JP28.1
  N26: part.LED_B, Q2.C, JP27.1
  N27: Q2.B, R7.Pin_0
  N28: Q3.B, R8.Pin_1
  N29: Q3.C, JP17.1, D1.anode, Water_Pump.pin_1, C8.-

custom parts:
  LCM1602 IIC: I2C-Module to use a 1602 or 2004 LCD on with the wire.h libory Serial LCD Modul
  TRANSISTOR_NPN: Generic NPN BJT. MMBT2222 is the common NPN we use. Double check against datasheet- not all devices are the same!
